// Logisim project processador_Bruno.circ as structural Verilog: 8 circuits, main circuit Add_4
module Main (
  input  [3:0] A,
  input  [3:0] B,
  input  [2:0] Controle,
  output out_4,
  output out_5,
  output [3:0] out_6
);

  wire decoder_1_s0, decoder_1_s1, decoder_1_s2, decoder_1_s4;
  wire [3:0] add_4_1_s, sub_4_1_s;

  Decoder decoder_1 (
    .in_1(Controle), .S0(decoder_1_s0), .S1(decoder_1_s1), .S2(decoder_1_s2), .S4(decoder_1_s4));  // open: S3, S5, S6, S7
  Buffer buffer_1 (.in_2(decoder_1_s0), .B(B), .S(out_6));
  Add_4 add_4_1 (.A(B), .Vai_1(out_5), .B(A), .Vem_1(1'b0), .S(add_4_1_s));
  Buffer buffer_2 (.in_2(decoder_1_s1), .B(add_4_1_s), .S(out_6));
  Sub_4 sub_4_1 (.A(B), .B(A), .Vem_1(1'b0), .Vai_1(out_4), .S(sub_4_1_s));
  Buffer buffer_3 (.in_2(decoder_1_s2), .B(sub_4_1_s), .S(out_6));
  Buffer_invertido buffer_invertido_1 (.B(B), .in_2(decoder_1_s4), .S(out_6));
endmodule

module Add_4 (
  input  [3:0] B,
  input  [3:0] A,
  input  Vem_1,
  output Vai_1,
  output [3:0] S
);

  wire add_1_2_vai_1, add_1_3_vai_1, add_1_4_vai_1;

  Add_1 add_1_1 (.s(S[3]), .vai_1(Vai_1), .A(A[3]), .B(B[3]), .Vem_1(add_1_2_vai_1));
  Add_1 add_1_2 (.s(S[2]), .vai_1(add_1_2_vai_1), .A(A[2]), .B(B[2]), .Vem_1(add_1_3_vai_1));
  Add_1 add_1_3 (.s(S[1]), .vai_1(add_1_3_vai_1), .A(A[1]), .B(B[1]), .Vem_1(add_1_4_vai_1));
  Add_1 add_1_4 (.s(S[0]), .vai_1(add_1_4_vai_1), .A(A[0]), .B(B[0]), .Vem_1(Vem_1));
endmodule

module Add_1 (
  input  A,
  input  B,
  input  Vem_1,
  output s,
  output vai_1
);

  wire and_1_out, and_2_out, or_1_out, xor_1_out;

  xor xor_1 (xor_1_out, A, B);
  or or_1 (or_1_out, B, Vem_1);
  and and_1 (and_1_out, B, Vem_1);
  xor xor_2 (s, xor_1_out, Vem_1);
  and and_2 (and_2_out, or_1_out, A);
  or or_2 (vai_1, and_2_out, and_1_out);
endmodule

module Sub_1 (
  input  A,
  input  B,
  input  Vem_1,
  output s,
  output vai_1
);

  wire and_1_out, and_2_out, not_1_out, or_1_out, xor_1_out;

  not not_1 (not_1_out, A);
  xor xor_1 (xor_1_out, A, B);
  or or_1 (or_1_out, B, Vem_1);
  and and_1 (and_1_out, B, Vem_1);
  xor xor_2 (s, xor_1_out, Vem_1);
  and and_2 (and_2_out, or_1_out, not_1_out);
  or or_2 (vai_1, and_2_out, and_1_out);
endmodule

module Sub_4 (
  input  [3:0] B,
  input  [3:0] A,
  input  Vem_1,
  output Vai_1,
  output [3:0] S
);

  wire sub_1_1_vai_1, sub_1_3_vai_1, sub_1_4_vai_1;

  Sub_1 sub_1_1 (.A(B[2]), .B(A[2]), .Vem_1(sub_1_3_vai_1), .s(S[2]), .vai_1(sub_1_1_vai_1));
  Sub_1 sub_1_2 (.A(B[3]), .B(A[3]), .Vem_1(sub_1_1_vai_1), .s(S[3]), .vai_1(Vai_1));
  Sub_1 sub_1_3 (.A(B[1]), .B(A[1]), .Vem_1(sub_1_4_vai_1), .s(S[1]), .vai_1(sub_1_3_vai_1));
  Sub_1 sub_1_4 (.A(B[0]), .B(A[0]), .Vem_1(Vem_1), .s(S[0]), .vai_1(sub_1_4_vai_1));
endmodule

module Buffer (
  input  [3:0] B,
  input  in_2,
  output [3:0] S
);

  assign S[3] = in_2 ? B[3] : 1'bz;  // Controlled_Buffer controlled_buffer_1
  assign S[2] = in_2 ? B[2] : 1'bz;  // Controlled_Buffer controlled_buffer_2
  assign S[0] = in_2 ? B[0] : 1'bz;  // Controlled_Buffer controlled_buffer_3
  assign S[1] = in_2 ? B[1] : 1'bz;  // Controlled_Buffer controlled_buffer_4
endmodule

module Buffer_invertido (
  input  [3:0] B,
  input  in_2,
  output [3:0] S
);

  assign S[1] = in_2 ? ~B[1] : 1'bz;  // Controlled_Inverter controlled_inverter_1
  assign S[3] = in_2 ? ~B[3] : 1'bz;  // Controlled_Inverter controlled_inverter_2
  assign S[2] = in_2 ? ~B[2] : 1'bz;  // Controlled_Inverter controlled_inverter_3
  assign S[0] = in_2 ? ~B[0] : 1'bz;  // Controlled_Inverter controlled_inverter_4
endmodule

module Decoder (
  input  [2:0] in_1,
  output S0,
  output S1,
  output S2,
  output S3,
  output S4,
  output S5,
  output S6,
  output S7
);

  wire not_1_out, not_2_out, not_3_out, not_4_out, not_5_out, not_6_out, not_7_out, not_8_out, not_9_out,
       not_10_out, not_11_out, not_12_out;

  not not_1 (not_1_out, in_1[2]);
  not not_2 (not_2_out, in_1[1]);
  not not_3 (not_3_out, in_1[0]);
  not not_4 (not_4_out, in_1[2]);
  not not_5 (not_5_out, in_1[1]);
  not not_6 (not_6_out, in_1[2]);
  not not_7 (not_7_out, in_1[0]);
  not not_8 (not_8_out, in_1[2]);
  not not_9 (not_9_out, in_1[1]);
  not not_10 (not_10_out, in_1[0]);
  not not_11 (not_11_out, in_1[1]);
  not not_12 (not_12_out, in_1[0]);
  and and_1 (S0, not_1_out, not_2_out, not_3_out);
  and and_2 (S1, not_4_out, not_5_out, in_1[0]);
  and and_3 (S2, not_6_out, in_1[1], not_7_out);
  and and_4 (S3, not_8_out, in_1[1], in_1[0]);
  and and_5 (S4, in_1[2], not_9_out, not_10_out);
  and and_6 (S5, in_1[2], not_11_out, in_1[0]);
  and and_7 (S6, in_1[2], in_1[1], not_12_out);
  and and_8 (S7, in_1[2], in_1[1], in_1[0]);
endmodule
